// Digital circuit 3a_reg_salida_restringida_4bits.dig as structural Verilog
module _3a_reg_salida_restringida_4bits (
  input  clk,
  input  [3:0] IN_4,
  input  en_o,
  input  W,
  output [3:0] out_d,
  output [3:0] out
);

  _2a_reg_salida_restringida_1bit _2a_reg_salida_restringida_1bit_1 (
    .in(IN_4[0]), .clk(clk), .en_out(en_o), .W(W), .out_d(out_d[0]), .out(out[0]));
  _2a_reg_salida_restringida_1bit _2a_reg_salida_restringida_1bit_2 (
    .in(IN_4[1]), .clk(clk), .en_out(en_o), .W(W), .out_d(out_d[1]), .out(out[1]));
  _2a_reg_salida_restringida_1bit _2a_reg_salida_restringida_1bit_3 (
    .in(IN_4[2]), .clk(clk), .en_out(en_o), .W(W), .out_d(out_d[2]), .out(out[2]));
  _2a_reg_salida_restringida_1bit _2a_reg_salida_restringida_1bit_4 (
    .in(IN_4[3]), .clk(clk), .en_out(en_o), .W(W), .out_d(out_d[3]), .out(out[3]));

  // Other names for the same wires on the sheet: en = en_o

  // Notes on the sheet:
  //   3a) Registro salida restringida - 4 bit
  //   habilitación de salida
  //   salida de debug
endmodule
