// Digital circuit 3b_ALU_registros_4bits.dig as structural Verilog
module _3b_ALU_registros_4bits (
  input  clk,
  input  [7:0] A,
  input  [7:0] B,
  input  Write_A,
  input  Write_B,
  input  [1:0] OP,
  input  en_out,
  output [7:0] a_2,
  output [7:0] b_2,
  output [7:0] S_debug,
  output [7:0] S,
  output C,
  output Z,
  output N,
  output V
);

  wire alu_completa_t_1_p7, alu_completa_t_1_p14, not_1_out, notconnected_1_out;
  wire [7:0] A_t, alu_completa_t_1_p12, B_t;

  _3a_reg_salida_restringida_4bits _3a_reg_salida_restringida_4bits_1 (
    .clk(clk), .IN_8(A), .en_o(1'b1), .W(Write_A), .out_d(a_2), .out(A_t));
  _3a_reg_salida_restringida_4bits _3a_reg_salida_restringida_4bits_2 (
    .clk(clk), .IN_8(B), .en_o(1'b1), .W(Write_B), .out_d(b_2), .out(B_t));
  // NotConnected on notconnected_1_out
  // ALU_completa_t alu_completa_t_1: pin names not known; wires that end beside it: a_2, notconnected_1_out, A_t, B_t, OP, b_2, alu_completa_t_1_p7, C, Z, N, V, alu_completa_t_1_p12, S, alu_completa_t_1_p14
  // NotConnected on alu_completa_t_1_p7
  not not_1 (not_1_out, clk);
  _3a_reg_salida_restringida_4bits _3a_reg_salida_restringida_4bits_3 (
    .clk(not_1_out), .IN_8(alu_completa_t_1_p12), .en_o(en_out), .W(1'b1), .out_d(S), .out(S_debug));
  // NotConnected on alu_completa_t_1_p14

  // Notes on the sheet:
  //   3b) ALU con registros de entrada y salida - 4 bits
endmodule
