// Digital circuit 3c_ALU_con_registros.dig as structural Verilog
module _3c_ALU_con_registros (
  input  clk,
  input  W0,
  input  W1,
  input  w_ALU_A,
  input  w_ALU_B,
  input  [1:0] OP,
  input  en_out_ALU,
  input  en_out_0,
  input  en_out_1,
  input  W2,
  input  en_out_2,
  input  W3,
  input  en_out_3,
  input  [7:0] Force_input,
  input  en_force_input,
  output [7:0] REG0,
  output [7:0] REG1,
  output C,
  output Z,
  output N,
  output V,
  output [7:0] REG2,
  output [7:0] REG3
);

  wire [7:0] _3a_reg_salida_restringida_4bits_1_out, _3b_alu_registros_4bits_1_a_2,
       _3b_alu_registros_4bits_1_b_2, _3b_alu_registros_4bits_1_s, driver_1_out;

  assign driver_1_out = en_force_input ? Force_input : 8'bz;  // Driver driver_1
  _3a_reg_salida_restringida_4bits _3a_reg_salida_restringida_4bits_1 (
    .clk(clk), .IN_8(driver_1_out), .en_o(en_out_0), .W(W0), .out_d(REG0),
    .out(_3a_reg_salida_restringida_4bits_1_out));
  _3a_reg_salida_restringida_4bits _3a_reg_salida_restringida_4bits_2 (
    .clk(clk), .IN_8(driver_1_out), .en_o(en_out_1), .W(W1), .out_d(REG1),
    .out(_3a_reg_salida_restringida_4bits_1_out));
  _3a_reg_salida_restringida_4bits _3a_reg_salida_restringida_4bits_3 (
    .clk(clk), .IN_8(driver_1_out), .en_o(en_out_2), .W(W2), .out_d(REG2),
    .out(_3a_reg_salida_restringida_4bits_1_out));
  _3a_reg_salida_restringida_4bits _3a_reg_salida_restringida_4bits_4 (
    .clk(clk), .IN_8(driver_1_out), .en_o(en_out_3), .W(W3), .out_d(REG3),
    .out(_3a_reg_salida_restringida_4bits_1_out));
  // NotConnected on nothing
  // NotConnected on nothing
  // NotConnected on nothing
  // NotConnected on nothing
  // NotConnected on nothing
  _3b_ALU_registros_4bits _3b_alu_registros_4bits_1 (
    .clk(clk), .A(_3a_reg_salida_restringida_4bits_1_out), .B(_3a_reg_salida_restringida_4bits_1_out),
    .Write_A(w_ALU_A), .Write_B(w_ALU_B), .OP(OP), .en_out(en_out_ALU), .a_2(_3b_alu_registros_4bits_1_a_2),
    .b_2(_3b_alu_registros_4bits_1_b_2), .S_debug(driver_1_out), .S(_3b_alu_registros_4bits_1_s), .C(C),
    .Z(Z), .N(N), .V(V));
  // NotConnected on nothing
  // NotConnected on nothing
  // NotConnected on nothing
  // NotConnected on nothing

  // Notes on the sheet:
  //   3c) Secuencia de operación ALU con registros y buses - 4 bits
  //   OP
  //   0 0
  //   0 1
  //   1 0
  //   1 1
  //   BUS 1
  //   ALU
  //   A  + B
  //   A  - B
  //   A  and B
  //   A  or B
  //   BUS 2
  //   OP
  //   =
endmodule
