// Digital circuit ALU_completa_t.dig as structural Verilog
module ALU_completa_t (
  input  [7:0] A,
  input  [7:0] B,
  input  [2:0] OP,
  output C,
  output Z,
  output N,
  output V,
  output [7:0] S
);

  wire notconnected_1_out;
  wire [3:0] unidad_aritmetica_t_1_s;
  wire [7:0] and_1_out, or_1_out;
  wire [7:4] unidad_aritmetica_t_1_s_2;

  assign and_1_out = B & A;  // And and_1, 8 bits wide
  assign or_1_out = B | A;  // Or or_1, 8 bits wide
  unidad_aritmetica_t unidad_aritmetica_t_1 (
    .A(A), .B(B), .OP(OP[1:0]), .S({unidad_aritmetica_t_1_s_2, unidad_aritmetica_t_1_s}), .C(C), .Z(Z),
    .N(N), .V(V));
  Multiplexer #(.Selector_Bits(2), .Bits(8)) multiplexer_1 (
    .sel(OP[2:1]), .in_2(and_1_out), .in_3(or_1_out), .out(S));  // open: in_0, in_1
  // NotConnected on notconnected_1_out
  Seven_Seg_Hex seven_seg_hex_1 (.d(unidad_aritmetica_t_1_s), .dp(C));
endmodule
