// Digital circuit unidad_aritmetica_t.dig as structural Verilog
module unidad_aritmetica_t (
  input  [7:0] A,
  input  [7:0] B,
  input  [2:0] OP,
  output [7:0] S,
  output C,
  output Z,
  output N,
  output V
);

  wire flag_overflow_t_1_v, not_1_out, O, sum_8bit_t_1_cout;
  wire [6:0] sum_8bit_t_1_s;
  wire [7:0] complementadora2_t_1_b, R;

  Multiplicacion multiplicacion_1 (.a(A), .b(B), .R(R), .O(O));
  complementadorA2_t complementadora2_t_1 (.B_2(B), .Neg(OP[0]), .B(complementadora2_t_1_b));
  sum_8bit_t sum_8bit_t_1 (
    .A(A), .B(complementadora2_t_1_b), .Cin(1'b0), .S({N, sum_8bit_t_1_s}), .Cout(sum_8bit_t_1_cout));
  not not_1 (not_1_out, sum_8bit_t_1_cout);
  flag_overflow_t flag_overflow_t_1 (.a3(A[7]), .b3(B[7]), .s3(N), .V(flag_overflow_t_1_v));
  Multiplexer multiplexer_1 (.sel(OP[0]), .in_0(sum_8bit_t_1_cout), .in_1(not_1_out), .out(C));
  flag_cero_t flag_cero_t_1 (.S({N, sum_8bit_t_1_s}), .Z(Z));
  Multiplexer multiplexer_2 (.sel(OP[2]), .in_0(flag_overflow_t_1_v), .in_1(O), .out(V));
  Multiplexer #(.Bits(8)) multiplexer_3 (.sel(OP[2]), .in_0({N, sum_8bit_t_1_s}), .in_1(R), .out(S));

  // Other names for the same wires on the sheet: OP_t = OP[2]
endmodule
